# Fritzing sketch Storymaker_gerber_pcb (saved by Fritzing 1.0.6)
circuit board: 8cm x 4.2cm

parts:
  LED = Screw terminal - 2 pins [package=THT]
  PULS = Screw terminal - 2 pins [package=THT]
  BAT = Screw terminal - 2 pins [package=THT]
  USB = Screw terminal - 2 pins [package=THT]
  INT = Screw terminal - 2 pins [package=THT]
  PRINT = screw terminal, 3 pins
  PI_ZERO_2W1 = screw terminal, 8 pins
  CARGADOR = screw terminal, 6 pins
  STEP-UP = screw terminal, 4 pins
  SPK = Screw terminal - 2 pins [package=THT]
  AUDIO = screw terminal, 7 pins

nets:
  N1: LED.pin1, PI_ZERO_2W1.pin1
  N2: LED.pin2, PULS.pin1, PRINT.pin3, PI_ZERO_2W1.pin6, CARGADOR.pin5, STEP-UP.pin1, STEP-UP.pin3, AUDIO.pin7
  N3: PULS.pin2, PI_ZERO_2W1.pin2
  N4: BAT.pin1, CARGADOR.pin4
  N5: BAT.pin2, CARGADOR.pin3
  N6: USB.pin1, CARGADOR.pin2
  N7: USB.pin2, CARGADOR.pin1
  N8: INT.pin1, CARGADOR.pin6
  N9: INT.pin2, STEP-UP.pin4
  N10: PRINT.pin1, PI_ZERO_2W1.pin8, STEP-UP.pin2, AUDIO.pin6
  N11: PRINT.pin2, PI_ZERO_2W1.pin7
  N12: PI_ZERO_2W1.pin3, AUDIO.pin5
  N13: PI_ZERO_2W1.pin4, AUDIO.pin4
  N14: PI_ZERO_2W1.pin5, AUDIO.pin3
  N15: SPK.pin1, AUDIO.pin2
  N16: SPK.pin2, AUDIO.pin1

notes:
  GND
  B-
  VOUT
  VIN
  OUT+
  OUT-
  Storymaker board V1.0
  +
  -
  5V IN
  B+
  5V
  GPIO14
  GPIO18
  GPIO19
  GPIO21
  GPIO23
  GPIO17
  BCLK
  LRC
  DIN
  S1
  Led+
  Tx
  P2
  P1
  S2
