# Fritzing sketch Storymaker_gerber_pin (saved by Fritzing 1.0.6)

parts:
  PULS = Screw terminal - 2 pins [package=THT]
  INT = Screw terminal - 2 pins [package=THT]
  BAT = Screw terminal - 2 pins [package=THT]
  SPK = Screw terminal - 2 pins [package=THT]
  USB = Screw terminal - 2 pins [package=THT]
  LED = Screw terminal - 2 pins [package=THT]
  PRINT = screw terminal, 3 pins
  PI_ZERO_2W1 = screw terminal, 8 pins
  AUDIO = screw terminal, 7 pins
  CARGADOR = screw terminal, 6 pins
  STEP-UP = screw terminal, 4 pins

nets:
  N1: PULS.pin1, LED.pin2, PRINT.pin3, PI_ZERO_2W1.pin6, AUDIO.pin7, CARGADOR.pin5, STEP-UP.pin1, STEP-UP.pin3
  N2: PULS.pin2, PI_ZERO_2W1.pin2
  N3: INT.pin1, CARGADOR.pin6
  N4: INT.pin2, STEP-UP.pin4
  N5: BAT.pin1, CARGADOR.pin4
  N6: BAT.pin2, CARGADOR.pin3
  N7: SPK.pin1, AUDIO.pin2
  N8: SPK.pin2, AUDIO.pin1
  N9: USB.pin1, CARGADOR.pin2
  N10: USB.pin2, CARGADOR.pin1
  N11: LED.pin1, PI_ZERO_2W1.pin1
  N12: PRINT.pin1, PI_ZERO_2W1.pin8, AUDIO.pin6, STEP-UP.pin2
  N13: PRINT.pin2, PI_ZERO_2W1.pin7
  N14: PI_ZERO_2W1.pin3, AUDIO.pin5
  N15: PI_ZERO_2W1.pin4, AUDIO.pin4
  N16: PI_ZERO_2W1.pin5, AUDIO.pin3
